# Fritzing sketch Light Mask Hardware (saved by Fritzing 0.9.2b)

parts:
  NEOPIXEL1 = Neopixel Strip -- White (30/m)
  Part1 = LightBlue Bean
  VCC1 = Battery

nets:
  GND: NEOPIXEL1.GND, Part1.GND, VCC1.-
  N1: NEOPIXEL1.Din, Part1.D4/MISO
  N2: NEOPIXEL1.+5V, VCC1.+

custom parts:
  Neopixel Strip -- White (30/m): These NeoPixel strips have 30 digitally-addressable pixel LEDs per meter and are very affordable and are only 12.5 mm wide, 10 mm if you remove the strip from the casing.
